// Logisim project mips_cpu.circ as structural Verilog: 15 circuits, main circuit main
module main (
);

  wire alu_1_equal, alu_circle_1_out_3, and_1_out, and_2_out, and_3_out, and_4_out, and_5_out, b27,
       clock_1_out, comparator_1_eq, IE, IM0, IM1, IM2, ir_circle_1_alusrc, ir_circle_1_branch,
       ir_circle_1_jal, ir_circle_1_jump, ir_circle_1_memread, ir_circle_1_memtoreg, ir_circle_1_memwrite,
       ir_circle_1_regdst, ir_circle_1_regwrite, ir_jr_1_jr, ir_jr_1_syscall, multiplexer_6_out, not_1_out,
       or_1_out;
  wire [2:0] ir_circle_1_aluop;
  wire [3:0] alu_circle_1_out_4;
  wire [4:0] multiplexer_1_out, multiplexer_2_out, wire_ir_1__15_11, wire_ir_1__20_16, wire_ir_1__25_21;
  wire [5:0] wire_ir_1__5_0, wire_ir_1__31_26;
  wire [9:0] alu_1_result_2;
  wire [15:0] multiplexer_9_out, wire_ir_1__15_0;
  wire [25:0] wire_ir_1__25_0;
  wire [29:0] bit_extender_1_out;
  wire [31:0] a0, adder_1_out, adder_2_out, alu_1_result, bit_extender_2_out, counter_1_q, extender_1_output,
       main_1_reg1, main_1_reg2_2, multiplexer_3_out, multiplexer_4_out, multiplexer_5_out,
       multiplexer_7_out, multiplexer_8_out, multiplexer_10_out, multiplexer_11_out, multiplexer_12_out,
       PC_q, ram_1_data, register_1_q, rom_1_data, v0;

  // Probe on multiplexer_12_out
  Register #(.width(32), .trigger("falling")) PC (
    .D(multiplexer_12_out), .en(1'b1), .Q(PC_q), .clk(and_3_out), .clr(1'b0));
  // Probe on v0
  Adder #(.width(32)) adder_1 (.a(32'h4), .b(PC_q), .out(adder_1_out), .cin(1'b0));  // open: cout
  Clock clock_1 (.out(clock_1_out));
  and and_1 (and_1_out, comparator_1_eq, ir_jr_1_syscall);
  Comparator #(.width(32)) comparator_1 (.a(v0), .b(32'ha), .eq(comparator_1_eq));  // open: gt, lt
  and and_2 (and_2_out, ~comparator_1_eq, ir_jr_1_syscall);  // AND_Gate
  ROM #(.addrWidth(10), .dataWidth(32)) rom_1 (.addr(PC_q[11:2]), .data(rom_1_data), .sel(1'b1));
  and and_3 (and_3_out, clock_1_out, ~and_1_out);  // AND_Gate
  cp0 cp0_1 (
    .IE(IE), .IM0(IM0), .IM1(IM1), .IM2(IM2));  // open: Reg1_num, Write_Reg_num, Din, Write_Enable, Clock, Reg1
  wire_ir wire_ir_1 (
    .\input (rom_1_data), ._25_0(wire_ir_1__25_0), ._15_0(wire_ir_1__15_0),
    ._31_26({wire_ir_1__31_26[5:2], b27, wire_ir_1__31_26[0]}), ._25_21(wire_ir_1__25_21),
    ._20_16(wire_ir_1__20_16), ._15_11(wire_ir_1__15_11), ._5_0(wire_ir_1__5_0));
  Register #(.width(32)) register_1 (.D(a0), .en(and_2_out), .Q(register_1_q), .clk(and_3_out));  // open: clr
  Multiplexer #(.width(5), .disabled(0), .enable("false")) multiplexer_1 (
    .in0(wire_ir_1__20_16), .in1(wire_ir_1__15_11), .out(multiplexer_1_out), .sel(ir_circle_1_regdst));
  Multiplexer #(.width(5), .disabled(0), .enable("false")) multiplexer_2 (
    .in0({5{1'b1}}), .in1(multiplexer_1_out), .out(multiplexer_2_out), .sel(ir_circle_1_jal));
  extender extender_1 (
    .\input (rom_1_data), .in_2({wire_ir_1__31_26[5:2], b27, wire_ir_1__31_26[0]}),
    .\output (extender_1_output));
  ir_jr ir_jr_1 (
    .in_1({wire_ir_1__31_26[5:2], b27, wire_ir_1__31_26[0]}), .in_2(wire_ir_1__5_0), .jr(ir_jr_1_jr),
    .syscall(ir_jr_1_syscall));
  Hex_Digit_Display hex_digit_display_1 (.value(register_1_q[31:28]));  // open: dp
  Hex_Digit_Display hex_digit_display_2 (.value(register_1_q[27:24]));  // open: dp
  interrupt interrupt_1 ();  // open: out_8, out_9, in_5, in_6, in_7, im0, im1, im2, ie
  IR_circle ir_circle_1 (
    .in_1({wire_ir_1__31_26[5:2], b27, wire_ir_1__31_26[0]}), .JAL(ir_circle_1_jal),
    .RegDst(ir_circle_1_regdst), .Branch(ir_circle_1_branch), .Jump(ir_circle_1_jump),
    .MemToReg(ir_circle_1_memtoreg), .MemRead(ir_circle_1_memread), .MemWrite(ir_circle_1_memwrite),
    .AluSrc(ir_circle_1_alusrc), .AluOp(ir_circle_1_aluop), .RegWrite(ir_circle_1_regwrite));
  Multiplexer #(.width(32), .disabled(0), .enable("false")) multiplexer_3 (
    .in0(adder_1_out), .in1(multiplexer_11_out), .out(multiplexer_3_out), .sel(ir_circle_1_jal));
  and and_4 (and_4_out, ~ir_jr_1_jr, ir_circle_1_regwrite);  // AND_Gate
  Hex_Digit_Display hex_digit_display_3 (.value(register_1_q[23:20]));  // open: dp
  Hex_Digit_Display hex_digit_display_4 (.value(register_1_q[19:16]));  // open: dp
  regfile_main main_1 (
    .Reg1_num(wire_ir_1__25_21), .Reg2(wire_ir_1__20_16), .Write_Reg_num(multiplexer_2_out),
    .Din(multiplexer_3_out), .Write_Enable(and_4_out), .Clock(and_3_out), .Reg1(main_1_reg1),
    .Reg2_2(main_1_reg2_2), .v0_Value(v0), .a0_Value(a0));  // open: s2_Value, ra_Value
  Hex_Digit_Display hex_digit_display_5 (.value(register_1_q[11:8]));  // open: dp
  Hex_Digit_Display hex_digit_display_6 (.value(register_1_q[15:12]));  // open: dp
  assign bit_extender_1_out = {{14{wire_ir_1__15_0[15]}}, wire_ir_1__15_0};  // Bit_Extender bit_extender_1
  Multiplexer #(.width(32), .disabled(0), .enable("false")) multiplexer_4 (
    .in0(main_1_reg2_2), .in1(extender_1_output), .out(multiplexer_4_out), .sel(or_1_out));
  or or_1 (or_1_out, ir_circle_1_alusrc, alu_circle_1_out_3);
  Hex_Digit_Display hex_digit_display_7 (.value(register_1_q[3:0]));  // open: dp
  Hex_Digit_Display hex_digit_display_8 (.value(register_1_q[7:4]));  // open: dp
  Multiplexer #(.width(32), .enable("false")) multiplexer_5 (
    .in0(main_1_reg1), .in1(main_1_reg2_2), .out(multiplexer_5_out), .sel(alu_circle_1_out_3));
  ALU alu_1 (
    .AluOP(alu_circle_1_out_4), .X(multiplexer_5_out), .Equal(alu_1_equal),
    .Result({alu_1_result[31:12], alu_1_result_2, alu_1_result[1:0]}), .Y(multiplexer_4_out));  // open: Signed_Overflow, Result_2, UnSigned_Overflow
  ALU_circle alu_circle_1 (
    .alu_op(ir_circle_1_aluop), .out_3(alu_circle_1_out_3), .out_4(alu_circle_1_out_4), .func(wire_ir_1__5_0));
  Multiplexer #(.select(2), .disabled(0), .enable("false")) multiplexer_6 (
    .in0(alu_1_equal), .in1(not_1_out), .in2(alu_1_result[0]), .out(multiplexer_6_out),
    .sel({b27, wire_ir_1__31_26[0]}));  // open: in3
  not not_1 (not_1_out, alu_1_equal);
  Adder #(.width(32)) adder_2 (
    .a(adder_1_out), .b({bit_extender_1_out, 2'b00}), .out(adder_2_out), .cin(1'b0));  // open: cout
  Counter #(.width(32), .max('hffffffff)) counter_1 (
    .count(1'b1), .Q(counter_1_q), .clk(and_3_out));  // open: load, D, carry, clr
  and and_5 (and_5_out, ir_circle_1_branch, multiplexer_6_out);
  // Probe on counter_1_q
  Multiplexer #(.width(32), .disabled(0), .enable("false")) multiplexer_7 (
    .in0(multiplexer_8_out), .in1({adder_1_out[31:28], wire_ir_1__25_0, 2'b00}), .out(multiplexer_7_out),
    .sel(ir_circle_1_jump));
  Multiplexer #(.width(32), .disabled(0), .enable("false")) multiplexer_8 (
    .in0(adder_1_out), .in1(adder_2_out), .out(multiplexer_8_out), .sel(and_5_out));
  RAM #(.addrWidth(10), .dataWidth(32), .bus("separate")) ram_1 (
    .addr(alu_1_result_2), .din(main_1_reg2_2), .data(ram_1_data), .str(ir_circle_1_memwrite), .sel(1'b1),
    .clk(and_3_out), .ld(ir_circle_1_memread), .clr(1'b0));
  Multiplexer #(.width(16), .disabled(0), .enable("false")) multiplexer_9 (
    .in0(ram_1_data[15:0]), .in1(ram_1_data[31:16]), .out(multiplexer_9_out), .sel(alu_1_result[1]));
  assign bit_extender_2_out = {{16{multiplexer_9_out[15]}}, multiplexer_9_out};  // Bit_Extender bit_extender_2
  Multiplexer #(.width(32), .disabled(0), .enable("false")) multiplexer_10 (
    .in0(bit_extender_2_out), .in1(ram_1_data), .out(multiplexer_10_out), .sel(b27));
  Multiplexer #(.width(32), .disabled(0), .enable("false")) multiplexer_11 (
    .in0({alu_1_result[31:12], alu_1_result_2, alu_1_result[1:0]}), .in1(multiplexer_10_out),
    .out(multiplexer_11_out), .sel(ir_circle_1_memtoreg));
  Multiplexer #(.width(32), .disabled(0), .enable("false")) multiplexer_12 (
    .in0(multiplexer_7_out), .in1(main_1_reg1), .out(multiplexer_12_out), .sel(ir_jr_1_jr));

  // Notes on the sheet:
  //   contents of rom_1 (hex, n*v repeats v):
  //   2009000a 1920fffe 94822 1920fffc
endmodule

module IR_circle (
  input  [5:0] in_1,
  output RegDst,
  output Branch,
  output Jump,
  output MemToReg,
  output MemRead,
  output MemWrite,
  output AluSrc,
  output [2:0] AluOp,
  output RegWrite,
  output JAL
);

  ir_1 ir_1_1 (
    .op1(in_1[5]), .op2(in_1[4]), .op3(in_1[3]), .op4(in_1[2]), .op5(in_1[1]), .op6(in_1[0]), .RegD(RegDst),
    .MemR(MemRead), .MemW(MemWrite));  // open: JrCt
  ir_2 ir_2_1 (
    .op1(in_1[5]), .op2(in_1[4]), .op3(in_1[3]), .op4(in_1[2]), .op5(in_1[1]), .op6(in_1[0]),
    .Branch(Branch), .Jmp(Jump), .RegWrite(RegWrite));
  ir_3 ir_3_1 (
    .op1(in_1[5]), .op2(in_1[4]), .op3(in_1[3]), .op4(in_1[2]), .op5(in_1[1]), .op6(in_1[0]),
    .MemTR(MemToReg), .AluSc(AluSrc));
  ir_4 ir_4_1 (
    .op1(in_1[5]), .op2(in_1[4]), .op3(in_1[3]), .op4(in_1[2]), .op5(in_1[1]), .op6(in_1[0]),
    .AluOp0(AluOp[2]), .AluOp1(AluOp[1]), .AluOp2(AluOp[0]));
  ir_jal ir_jal_1 (
    .op6(in_1[5]), .op5(in_1[4]), .op4(in_1[3]), .op3(in_1[2]), .op2(in_1[1]), .op1(in_1[0]), .out1(JAL));
endmodule

module ALU_circle (
  input  [2:0] alu_op,
  input  [5:0] func,
  output out_3,
  output [3:0] out_4
);

  alu_1 alu_1_1 (
    .op3(alu_op[2]), .op2(alu_op[1]), .op1(alu_op[0]), .fun6(func[5]), .fun5(func[4]), .fun4(func[3]),
    .fun3(func[2]), .fun2(func[1]), .fun1(func[0]), .out4(out_4[3]), .out3(out_4[2]), .out2(out_4[1]),
    .out1(out_4[0]), .shift(out_3));
endmodule

module ir_2 (
  input  op1,
  input  op2,
  input  op3,
  input  op4,
  input  op5,
  input  op6,
  output Branch,
  output Jmp,
  output RegWrite
);

  wire and_2_out, and_3_out, and_4_out, and_5_out, and_6_out, and_7_out, not_1_out, not_2_out, not_3_out,
       not_4_out, not_5_out, not_6_out, not_7_out, not_8_out, not_9_out, not_10_out, not_11_out, not_12_out,
       not_13_out;

  not not_1 (not_1_out, op3);
  not not_2 (not_2_out, op1);
  not not_3 (not_3_out, op3);
  not not_4 (not_4_out, op4);
  not not_5 (not_5_out, op1);
  not not_6 (not_6_out, op3);
  not not_7 (not_7_out, op1);
  not not_8 (not_8_out, op3);
  not not_9 (not_9_out, op4);
  not not_10 (not_10_out, op5);
  not not_11 (not_11_out, op3);
  not not_12 (not_12_out, op4);
  not not_13 (not_13_out, op1);
  and and_1 (Branch, not_1_out, op4);
  and and_2 (and_2_out, not_2_out, not_3_out, not_4_out, op5);
  and and_3 (and_3_out, not_5_out, not_6_out, op5, op6);
  and and_4 (and_4_out, not_7_out, op2, not_8_out, op5);
  and and_5 (and_5_out, not_9_out, not_10_out);
  and and_6 (and_6_out, not_11_out, not_12_out, op6);
  and and_7 (and_7_out, not_13_out, op3);
  or or_1 (Jmp, and_2_out, and_3_out, and_4_out);
  or or_2 (RegWrite, and_5_out, and_6_out, and_7_out);
endmodule

module ir_3 (
  input  op1,
  input  op2,
  input  op3,
  input  op4,
  input  op5,
  input  op6,
  output MemTR,
  output AluSc
);

  wire and_1_out, and_2_out, and_3_out, not_1_out;

  not not_1 (not_1_out, op2);
  and and_1 (and_1_out, op2, op4);
  and and_2 (and_2_out, op1, not_1_out, op6);
  and and_3 (and_3_out, op1, op4);
  or or_1 (AluSc, op5, op3, and_1_out, and_2_out, and_3_out);

  assign MemTR = op1;
endmodule

module ir_4 (
  input  op1,
  input  op2,
  input  op3,
  input  op4,
  input  op5,
  input  op6,
  output AluOp0,
  output AluOp1,
  output AluOp2
);

  wire and_2_out, and_3_out, and_4_out, and_5_out, and_6_out, and_7_out, and_8_out, not_1_out, not_2_out,
       not_3_out, not_4_out, not_5_out, not_6_out, not_7_out, not_8_out, not_9_out, not_10_out, not_11_out,
       not_12_out, not_13_out, not_14_out, not_15_out, not_16_out, not_17_out;

  not not_1 (not_1_out, op1);
  not not_2 (not_2_out, op2);
  not not_3 (not_3_out, op3);
  not not_4 (not_4_out, op5);
  not not_5 (not_5_out, op1);
  not not_6 (not_6_out, op2);
  not not_7 (not_7_out, op3);
  not not_8 (not_8_out, op6);
  not not_9 (not_9_out, op6);
  and and_1 (AluOp1, op3, op4);
  not not_10 (not_10_out, op2);
  not not_11 (not_11_out, op3);
  not not_12 (not_12_out, op5);
  not not_13 (not_13_out, op2);
  not not_14 (not_14_out, op3);
  not not_15 (not_15_out, op6);
  not not_16 (not_16_out, op4);
  not not_17 (not_17_out, op5);
  and and_2 (and_2_out, not_1_out, not_2_out, not_3_out, op4, not_4_out);
  and and_3 (and_3_out, not_5_out, not_6_out, not_7_out, op4, not_8_out);
  and and_4 (and_4_out, op3, op5, not_9_out);
  and and_5 (and_5_out, not_10_out, not_11_out, op4, not_12_out);
  and and_6 (and_6_out, not_13_out, not_14_out, op4, not_15_out);
  and and_7 (and_7_out, op3, not_16_out, not_17_out);
  and and_8 (and_8_out, op3, op6);
  or or_1 (AluOp0, and_2_out, and_3_out, and_4_out);
  or or_2 (AluOp2, and_5_out, and_6_out, and_7_out, and_8_out, op1);
endmodule

module ir_1 (
  input  op1,
  input  op2,
  input  op3,
  input  op4,
  input  op5,
  input  op6,
  output JrCt,
  output RegD,
  output MemR,
  output MemW
);

  wire and_2_out, and_3_out, and_4_out, and_5_out, not_1_out, not_2_out, not_3_out, not_4_out, not_5_out,
       not_6_out, not_7_out, not_8_out, not_9_out, not_10_out, not_11_out, not_12_out, not_13_out,
       not_14_out, not_15_out, not_16_out;

  not not_1 (not_1_out, op1);
  not not_2 (not_2_out, op2);
  not not_3 (not_3_out, op3);
  not not_4 (not_4_out, op4);
  not not_5 (not_5_out, op1);
  not not_6 (not_6_out, op3);
  not not_7 (not_7_out, op5);
  not not_8 (not_8_out, op3);
  not not_9 (not_9_out, op5);
  not not_10 (not_10_out, op6);
  not not_11 (not_11_out, op3);
  not not_12 (not_12_out, op5);
  not not_13 (not_13_out, op3);
  not not_14 (not_14_out, op5);
  not not_15 (not_15_out, op2);
  not not_16 (not_16_out, op4);
  and and_1 (JrCt, not_1_out, not_2_out, not_3_out, not_4_out, op5, op6);
  and and_2 (and_2_out, not_5_out, not_6_out, not_7_out);
  and and_3 (and_3_out, not_8_out, not_9_out, not_10_out);
  and and_4 (and_4_out, not_11_out, op4, not_12_out);
  and and_5 (and_5_out, op2, not_13_out, not_14_out);
  and and_6 (MemW, op1, not_15_out, op3, not_16_out, op5, op6);
  or or_1 (RegD, and_2_out, and_3_out, and_4_out, and_5_out);

  assign MemR = op1;
endmodule

module alu_1 (
  input  op3,
  input  op2,
  input  op1,
  input  fun6,
  input  fun5,
  input  fun4,
  input  fun3,
  input  fun2,
  input  fun1,
  output out4,
  output out3,
  output out2,
  output out1,
  output shift
);

  wire and_1_out, and_2_out, and_3_out, and_4_out, and_5_out, and_6_out, and_7_out, and_8_out, and_9_out,
       and_10_out, and_11_out, and_12_out, and_13_out, and_14_out, and_15_out, and_16_out, and_17_out,
       and_18_out, and_19_out, and_20_out, and_21_out, and_22_out, and_23_out, and_24_out, and_25_out,
       and_26_out, not_1_out, not_2_out, not_3_out, not_4_out, not_5_out, not_6_out, not_7_out, not_8_out,
       not_9_out, not_10_out, not_11_out, not_12_out, not_13_out, not_14_out, not_15_out, not_16_out,
       not_17_out, not_18_out, not_19_out, not_20_out, not_21_out, not_22_out, not_23_out, not_24_out,
       not_25_out, not_26_out, not_27_out, not_28_out, not_29_out, not_30_out, not_31_out, not_32_out,
       not_33_out, not_34_out, not_35_out, not_36_out, not_37_out, not_38_out, not_39_out, not_40_out,
       not_41_out, not_42_out, not_43_out, not_44_out, not_45_out, not_46_out, not_47_out, not_48_out,
       not_49_out, not_50_out, not_51_out, not_52_out, not_53_out, not_54_out, not_55_out, not_56_out,
       not_57_out, not_58_out, not_59_out, not_60_out, not_61_out, not_62_out, not_63_out, not_64_out,
       not_65_out, or_1_out;

  not not_1 (not_1_out, op2);
  not not_2 (not_2_out, op1);
  not not_3 (not_3_out, fun6);
  not not_4 (not_4_out, fun5);
  not not_5 (not_5_out, fun2);
  not not_6 (not_6_out, op2);
  not not_7 (not_7_out, op1);
  not not_8 (not_8_out, op2);
  not not_9 (not_9_out, op1);
  not not_10 (not_10_out, op3);
  not not_11 (not_11_out, op2);
  not not_12 (not_12_out, fun1);
  not not_13 (not_13_out, op3);
  not not_14 (not_14_out, op2);
  not not_15 (not_15_out, fun6);
  not not_16 (not_16_out, fun5);
  not not_17 (not_17_out, fun4);
  not not_18 (not_18_out, op3);
  not not_19 (not_19_out, op2);
  not not_20 (not_20_out, fun4);
  not not_21 (not_21_out, fun3);
  not not_22 (not_22_out, op3);
  not not_23 (not_23_out, op2);
  not not_24 (not_24_out, fun5);
  not not_25 (not_25_out, fun3);
  not not_26 (not_26_out, op2);
  not not_27 (not_27_out, op1);
  not not_28 (not_28_out, op1);
  not not_29 (not_29_out, fun1);
  not not_30 (not_30_out, op1);
  not not_31 (not_31_out, op1);
  not not_32 (not_32_out, fun1);
  not not_33 (not_33_out, op1);
  not not_34 (not_34_out, fun1);
  not not_35 (not_35_out, op1);
  not not_36 (not_36_out, fun1);
  not not_37 (not_37_out, op1);
  not not_38 (not_38_out, op2);
  not not_39 (not_39_out, fun4);
  not not_40 (not_40_out, fun3);
  not not_41 (not_41_out, op2);
  not not_42 (not_42_out, fun5);
  not not_43 (not_43_out, fun2);
  not not_44 (not_44_out, fun1);
  not not_45 (not_45_out, op2);
  not not_46 (not_46_out, fun6);
  not not_47 (not_47_out, op2);
  not not_48 (not_48_out, fun2);
  not not_49 (not_49_out, op2);
  not not_50 (not_50_out, fun1);
  not not_51 (not_51_out, op2);
  not not_52 (not_52_out, op2);
  not not_53 (not_53_out, op2);
  not not_54 (not_54_out, fun2);
  not not_55 (not_55_out, fun1);
  not not_56 (not_56_out, op2);
  not not_57 (not_57_out, op1);
  not not_58 (not_58_out, fun1);
  and and_1 (and_1_out, not_1_out, not_2_out, not_3_out, not_4_out, fun3, not_5_out);
  and and_2 (and_2_out, not_6_out, not_7_out, fun3, fun1);
  and and_3 (and_3_out, not_8_out, not_9_out, fun4);
  and and_4 (and_4_out, op2, op1);
  and and_5 (and_5_out, not_10_out, not_11_out, fun3, not_12_out);
  and and_6 (and_6_out, not_13_out, not_14_out, not_15_out, not_16_out, not_17_out, fun3, fun2);
  and and_7 (and_7_out, not_18_out, not_19_out, fun6, not_20_out, not_21_out);
  and and_8 (and_8_out, not_22_out, not_23_out, fun6, not_24_out, not_25_out, fun2, fun1);
  and and_9 (and_9_out, not_26_out, op1);
  and and_10 (and_10_out, op2, not_27_out);
  and and_11 (and_11_out, not_28_out, fun2, not_29_out);
  and and_12 (and_12_out, not_30_out, fun3, fun2);
  and and_13 (and_13_out, not_31_out, fun4, fun3, not_32_out);
  and and_14 (and_14_out, not_33_out, fun5, fun3, not_34_out);
  and and_15 (and_15_out, not_35_out, fun6, fun3, not_36_out);
  and and_16 (and_16_out, op2, not_37_out);
  and and_17 (and_17_out, not_38_out, not_39_out, not_40_out, fun1);
  and and_18 (and_18_out, not_41_out, not_42_out, fun3, not_43_out, not_44_out);
  and and_19 (and_19_out, not_45_out, not_46_out, fun4);
  and and_20 (and_20_out, not_47_out, fun4, not_48_out);
  and and_21 (and_21_out, not_49_out, fun4, not_50_out);
  and and_22 (and_22_out, not_51_out, fun4, fun3);
  and and_23 (and_23_out, not_52_out, fun5, fun4);
  and and_24 (and_24_out, not_53_out, fun6, not_54_out, not_55_out);
  and and_25 (and_25_out, not_56_out, op1);
  and and_26 (and_26_out, op2, not_57_out);
  not not_59 (not_59_out, op3);
  not not_60 (not_60_out, op2);
  not not_61 (not_61_out, op1);
  not not_62 (not_62_out, fun6);
  not not_63 (not_63_out, fun5);
  not not_64 (not_64_out, fun4);
  not not_65 (not_65_out, fun3);
  or or_1 (or_1_out, fun2, not_58_out);
  or or_2 (out4, and_1_out, and_2_out, and_3_out, and_4_out, op3);
  or or_3 (out3, and_5_out, and_6_out, and_7_out, and_8_out, and_9_out, and_10_out);
  or or_4 (out2, and_11_out, and_12_out, and_13_out, and_14_out, and_15_out, and_16_out, op3);
  or or_5 (out1, and_17_out, and_18_out, and_19_out, and_20_out, and_21_out, and_22_out, and_23_out, and_24_out, and_25_out, and_26_out, op3);
  and and_27 (shift, not_59_out, not_60_out, not_61_out, not_62_out, not_63_out, not_64_out, not_65_out, or_1_out);
endmodule

module extender (
  input  [31:0] \input ,
  input  [5:0] in_2,
  output [31:0] \output 
);

  wire [1:0] ext_ctrl_1_out1;
  wire [31:0] bit_extender_1_out, bit_extender_2_out, bit_extender_3_out;

  assign bit_extender_1_out = {{16{1'b0}}, \input [15:0]};  // Bit_Extender bit_extender_1
  assign bit_extender_2_out = {{16{\input [15]}}, \input [15:0]};  // Bit_Extender bit_extender_2
  assign bit_extender_3_out = {{27{\input [10]}}, \input [10:6]};  // Bit_Extender bit_extender_3
  ext_ctrl ext_ctrl_1 (
    .op6(in_2[5]), .op5(in_2[4]), .op4(in_2[3]), .op3(in_2[2]), .op2(in_2[1]), .op1(in_2[0]),
    .out2(ext_ctrl_1_out1[1]), .out1(ext_ctrl_1_out1[0]));
  Multiplexer #(.select(2), .width(32), .disabled(0), .enable("false")) multiplexer_1 (
    .in0(bit_extender_1_out), .in1(bit_extender_2_out), .in2(bit_extender_3_out), .out(\output ),
    .sel(ext_ctrl_1_out1));  // open: in3

  // Notes on the sheet:
  //   us[15:0]
  //   s[15:0]
  //   s[10:6]
endmodule

module ext_ctrl (
  input  op6,
  input  op5,
  input  op4,
  input  op3,
  input  op2,
  input  op1,
  output out2,
  output out1
);

  wire and_1_out, and_2_out, and_3_out, and_4_out, and_5_out, not_1_out, not_2_out, not_3_out, not_4_out,
       not_5_out, not_6_out, not_7_out, not_8_out, not_9_out, not_10_out, not_11_out, not_12_out, not_13_out,
       not_14_out;

  not not_1 (not_1_out, op6);
  not not_2 (not_2_out, op4);
  not not_3 (not_3_out, op3);
  not not_4 (not_4_out, op2);
  not not_5 (not_5_out, op4);
  not not_6 (not_6_out, op3);
  not not_7 (not_7_out, op2);
  not not_8 (not_8_out, op1);
  not not_9 (not_9_out, op4);
  not not_10 (not_10_out, op3);
  not not_11 (not_11_out, op2);
  not not_12 (not_12_out, op1);
  not not_13 (not_13_out, op5);
  not not_14 (not_14_out, op4);
  and and_1 (and_1_out, not_1_out, not_2_out, not_3_out, not_4_out);
  and and_2 (and_2_out, not_5_out, not_6_out, not_7_out, not_8_out);
  and and_3 (and_3_out, op5, not_9_out, not_10_out, not_11_out);
  and and_4 (and_4_out, op4, not_12_out);
  and and_5 (and_5_out, op6, not_13_out, not_14_out, op1);
  or or_1 (out2, and_1_out, and_2_out, and_3_out);
  or or_2 (out1, op2, op3, and_4_out, and_5_out);
endmodule

module ir_jal (
  input  op6,
  input  op5,
  input  op4,
  input  op3,
  input  op2,
  input  op1,
  output out1
);

  wire not_1_out, not_2_out;

  not not_1 (not_1_out, op2);
  not not_2 (not_2_out, op1);
  or or_1 (out1, not_1_out, not_2_out, op3, op4, op5, op6);
endmodule

module ir_jr (
  input  [5:0] in_1,
  input  [5:0] in_2,
  output jr,
  output syscall
);

  wire not_1_out, not_2_out, not_3_out, not_4_out, not_5_out, not_6_out, not_7_out, not_8_out, not_9_out,
       not_10_out, not_11_out;

  not not_1 (not_1_out, in_1[5]);
  not not_2 (not_2_out, in_1[4]);
  not not_3 (not_3_out, in_1[3]);
  not not_4 (not_4_out, in_1[2]);
  not not_5 (not_5_out, in_1[1]);
  not not_6 (not_6_out, in_1[0]);
  not not_7 (not_7_out, in_2[5]);
  not not_8 (not_8_out, in_2[4]);
  not not_9 (not_9_out, in_2[2]);
  not not_10 (not_10_out, in_2[1]);
  not not_11 (not_11_out, in_2[0]);
  and and_1 (jr, not_1_out, not_2_out, not_3_out, not_4_out, not_5_out, not_6_out, not_7_out, not_8_out, in_2[3], not_9_out, not_10_out, not_11_out);
  and and_2 (syscall, not_1_out, not_2_out, not_3_out, not_4_out, not_5_out, not_6_out, not_7_out, not_8_out, in_2[3], in_2[2], not_10_out, not_11_out);
endmodule

module wire_ir (
  input  [31:0] \input ,
  output [25:0] _25_0,
  output [15:0] _15_0,
  output [5:0] _31_26,
  output [4:0] _25_21,
  output [4:0] _20_16,
  output [4:0] _15_11,
  output [5:0] _5_0
);


  assign _5_0 = \input [5:0];
  assign _15_0 = \input [15:0];
  assign _15_11 = \input [15:11];
  assign _20_16 = \input [20:16];
  assign _25_0 = \input [25:0];
  assign _25_21 = \input [25:21];
  assign _31_26 = \input [31:26];
endmodule

module cp0 (
  input  [4:0] Reg1_num,
  input  [4:0] Write_Reg_num,
  input  [31:0] Din,
  input  Write_Enable,
  input  Clock,
  output [31:0] Reg1,
  output IE,
  output IM0,
  output IM1,
  output IM2
);

  wire decoder_1_out0, decoder_1_out1;
  wire [31:0] EPC_q;
  wire [31:4] SR_q;

  Decoder #(.disabled(0)) decoder_1 (
    .out0(decoder_1_out0), .out1(decoder_1_out1), .sel(Write_Reg_num[0]), .en(Write_Enable));
  Register #(.width(32)) SR (.D(Din), .en(decoder_1_out0), .Q({SR_q, IM2, IM1, IM0, IE}), .clk(Clock));  // open: clr
  Register #(.width(32)) EPC (.D(Din), .en(decoder_1_out1), .Q(EPC_q), .clk(Clock));  // open: clr
  Multiplexer #(.width(32), .disabled(0), .enable("false")) multiplexer_1 (
    .in0({SR_q, IM2, IM1, IM0, IE}), .in1(EPC_q), .out(Reg1), .sel(Reg1_num[0]));

  // Other names for the same wires on the sheet: clk = Clock; WE = Write_Enable; write_data[31:0] = Din

  // Notes on the sheet:
  //   输入引脚
  //   输出引脚
endmodule

module interrupt (
  input  im0,
  input  im1,
  input  im2,
  input  ie,
  input  in_5,
  input  in_6,
  input  in_7,
  output [1:0] out_8,
  output out_9
);

  wire and_1_out, and_2_out, and_3_out, d_ff_1_q, d_ff_2_q, d_ff_3_q, undriven;

  Counter #(.width(1), .max('h1)) counter_1 ();  // open: load, D, count, Q, carry, clk, clr
  Priority_Encoder #(.select(2)) priority_encoder_1 (
    .in0(and_1_out), .in1(and_2_out), .in2(and_3_out), .out(out_8));  // open: in3
  and and_1 (and_1_out, d_ff_1_q, ~im0);  // AND_Gate
  D_Flip_Flop d_ff_1 (.Q(d_ff_1_q), .preset(in_5), .en(1'b0));  // open: clk, D, Qn, reset
  and and_2 (and_2_out, d_ff_2_q, ~im1);  // AND_Gate
  D_Flip_Flop d_ff_2 (.Q(d_ff_2_q), .preset(in_6), .en(1'b0));  // open: clk, D, Qn, reset
  and and_3 (and_3_out, d_ff_3_q, ~im2);  // AND_Gate
  D_Flip_Flop d_ff_3 (.Q(d_ff_3_q), .preset(in_7), .en(1'b0));  // open: clk, D, Qn, reset
  and and_4 (out_9, undriven, ie);
endmodule
